# Fritzing sketch Package (saved by Fritzing 0.9.3b)
circuit board: 12.8cm x 11cm
breadboards: 1

parts:
  Part1 = Adafruit Feather M0 Adalogger [part_number="Feather M0"]
  Part2 = Adafruit RFM9x LoRa Radio [part_number="RFM9x LoRa"]
  Part3 = Adafruit TSL2561 [part_number="Adafruit #439"]
  Part4 = Adafruit TSL2561 [part_number="Adafruit #439"]
  Part5 = Adafruit TSL2561 [part_number="Adafruit #439"]
  Part6 = 9-DOF Absolute Orientation IMU Fusion Breakout - BNO055 [part_number=BNO055]
  Part7 = Adafruit Mini Relay FeatherWing [part_number="Adafruit #2895"]
  Part8 = Adafruit LM3671 Buck Converter [part_number="LM3671 Buck Converter"]
  J2 = female pin header, 5 pins [form="♀ (female)" part_number="Geiger 2"]
  J3 = Screw terminal - 2 pins [part_number="Power Terminal" package=THT]
  U1 = COPERNICUS-DIP [part_number="Copernicus GPS" package=copernicus-dip]
  J1 = female pin header, 5 pins [form="♀ (female)" part_number="Geiger 1"]
  Part9 = Adafruit MAX31865 RTD Sensor Breakout [part_number="MAX31865 RTD Breakout"]
  R1 = Resistor [tolerance=±5% resistance=5k package=THT]
  R2 = Resistor [tolerance=±5% resistance=5k package=THT]
  J4 = female pin header, 1 pin [form="♀ (female)" part_number="Relay SIgnal Header"]
  Part10 = Arduino Uno (Rev3)  # not connected

nets:
  GND: Part1.GND, Part2.GND, Part3.GND, Part4.GND, Part5.GND, Part5.ADDR, Part6.GND, Part7.GND, Part8.GND, J2.pin2, J2.pin4, J3.pin1, U1.GND, J1.pin2, J1.pin4, Part9.GND
  N1: Part1.D1, U1.RXD-B
  N2: Part1.D0, U1.TXD-B
  N3: Part1.MISO, Part2.MISO
  N4: Part1.MOSI, Part2.MOSI
  N5: Part1.SCK, Part2.SCK
  N6: Part1.A4, Part9.SCLK
  N7: Part1.A3, Part9.SDO
  N8: Part1.A2, Part9.SDI
  N9: Part1.A1, Part9.CS
  N10: Part1.D13, J2.pin1
  N11: Part1.D12, J2.pin3
  N12: Part1.D11, J1.pin1
  N13: Part1.D10, J1.pin3
  N14: Part1.D9, Part2.DIO0
  N15: Part1.D6, Part2.RST
  N16: Part1.D5, Part2.CS
  SCL: Part1.SCL, Part3.SCL, Part4.SCL, Part5.SCL, Part6.SCL_5V, R2.Pin_0
  SDA: Part1.SDA, Part3.SDA, Part4.SDA, Part5.SDA, Part6.SDA_5V, R1.Pin_0
  3.3V: Part2.VIN, Part3.VIN, Part4.VIN, Part4.ADDR, Part5.VIN, Part6.5.0V, Part7.3.3V, Part8.3.3V, J2.pin5, J1.pin5
  N17: Part7.EN, J4.pin1
  7.2V: Part8.VIN, J3.pin2
  VCC: U1.VCC, Part9.VIN, R1.Pin_1, R2.Pin_1

notes:
  GND
  BATT+
  BNO
  RELAY
  LM3671
  LoRa
  GPS
  MAX31865 RTD
  Lux Hi
  Lux Lo
  Lux Ft
  Geiger 1
  Geiger 2

custom parts:
  Adafruit Feather M0 Adalogger: This is the Adafruit Feather M0 Adalogger - our take on an 'all-in-one' Cortex M0 datalogger (or data-reader) with built in USB and battery charging. Its an Adafruit Feather M0 with a microSD holder ready to rock! We have other boards in the Feather family, check'em out here At the Feather M0's heart is an ATSAMD21G18 ARM Cortex M0 processor, clocked at 48 MHz and at 3.3V logic, the same one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
  Adafruit RFM9x LoRa Radio: Sending data over long distances is like magic, and now you can be a magician with this range of powerful and easy-to-use radio modules. Sure, sometimes you want to talk to a computer (a good time to use WiFi) or perhaps communicate with a Phone (choose Bluetooth Low Energy!) but what if you want to send data very far? Most WiFi, Bluetooth, Zigbee and other wireless chipsets use 2.4GHz, which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
  Adafruit TSL2561: The TSL2561 luminosity sensor is an advanced digital light sensor, ideal for use in a wide range of light situations. Compared to low cost CdS cells, this sensor is more precise, allowing for exact lux calculations and can be configured for different gain/timing ranges to detect light ranges from up to 0.1 - 40,000+ Lux on the fly. The best part of this sensor is that it contains both infrared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
  9-DOF Absolute Orientation IMU Fusion Breakout - BNO055: A MEMS accelerometer, magnetometer and gyroscope on a single die with a high speed ARM Cortex-M0 based processor to digest all the sensor data, abstract the sensor fusion and real time requirements away, and spit out data you can use in quaternions, Euler angles or vectors.
  Adafruit Mini Relay FeatherWing: A Feather board without ambition is a Feather board without FeatherWings! This is the Non-Latching Mini Relay FeatherWing. It gives you power to control, and control over power. Put simply, you can now turn on and off lamps, fans, solenoids, and other small appliances that run on up to 250VAC or DC power using any Feather board. The are two 'flavors' of these FeatherWings, this is the simple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
  Adafruit LM3671 Buck Converter: Your power supply problems just got SUPER SOLVED! This 3.3V Buck Converter Breakout board is great for supplying power to low voltage circuits from a single Li-Ion cell battery or USB power. This chip provides up to 600-mA load current across the entire input voltage range of 3.5 to 5.5V. Great for your portable project, we made this "pin compatible" with the LM1117-3.3V TO-220 chip so you can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
  Adafruit MAX31865 RTD Sensor Breakout: For precision temperature sensing, nothing beats a Platinum RTD. Resistance temperature detectors (RTDs) are temperature sensors that contain a resistor that changes resistance value as its temperature changes, basically a kind of thermistor. In this sensor, the resistor is actually a small strip of Platinum with a resistance of 100 ohms at 0°C, thus the name PT100. Compared to most NTC/PTC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
